# Fritzing sketch complete_schema_doit_esp_devkit (saved by Fritzing 0.9.6b)
breadboards: 2

parts:
  M1 = DOIT Esp32 DevKit v1 (30 pins long, 11 pins width) [part_number=ESP32S-PIN30]
  S2 = SWITCH-MOMENTARY-2 [package=tactile-pth-12mm]
  S3 = SWITCH-MOMENTARY-2 [package=tactile-pth-12mm]
  S4 = SWITCH-MOMENTARY-2 [package=tactile-pth-12mm]
  S5 = SWITCH-MOMENTARY-2 [package=tactile-pth-12mm]
  Grove1 = Grove OLED 128x96
  U1 = PCF8574 [package="DIP16 [THT]"]
  Matrix_keypad1 = KEYPAD 4x4
  switch1 = Rotary_Switch_12x1

nets (from the breadboard view):
  3V3: M1.3V3, U1.VCC
  GND: M1.GND, S2.1, S3.1, S4.1, S5.1, Grove1.GND, U1.GND, switch1.0
  N1: M1.D5, switch1.6
  N2: M1.D18, switch1.7
  N3: M1.D19, switch1.8
  N4: M1.D21, switch1.9
  N5: M1.D22, Grove1.SDA, U1.SDA
  N6: M1.D23, Grove1.SCL, U1.SCL
  N7: M1.D25, S4.2
  N8: M1.D26, S5.2
  N9: M1.D27, S2.2
  N10: M1.D14, S3.2
  N11: U1.P0, Matrix_keypad1.row1
  N12: U1.P1, Matrix_keypad1.row2
  N13: U1.P2, Matrix_keypad1.row3
  N14: U1.P3, Matrix_keypad1.row4
  N15: U1.P4, Matrix_keypad1.col1
  N16: U1.P5, Matrix_keypad1.col2
  N17: U1.P6, Matrix_keypad1.col3
  N18: U1.P7, Matrix_keypad1.col4

custom parts:
  DOIT Esp32 DevKit v1 (30 pins long, 11 pins width): The DOIT Esp32 DevKit v1 is one of the development board created by DOIT to evaluate the ESP-WROOM-32 module. It is based on the ESP32 microcontroller that boasts Wifi, Bluetooth, Ethernet and Low Power support all in a single chip. (vanepp) made breadboard work, adjusted pin numbering and labels and reduced size of schematic and cleaned up pcb. This chip is 30pins long (2 x15) and 11 pins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
  KEYPAD 4x4: Matrix keypad 16 buttons, 4 rows x 4 columns
